// Logisim project 1_bit_mem_cell.circ as structural Verilog: 1 circuit, main circuit main
module main (
  input  set,
  input  enable,
  output q
);

  wire nand_1_out, nand_2_out, nand_4_out, not_1_out;

  not not_1 (not_1_out, set);
  nand nand_1 (nand_1_out, set, enable);
  nand nand_2 (nand_2_out, enable, not_1_out);
  nand nand_3 (q, nand_1_out, nand_4_out);
  nand nand_4 (nand_4_out, q, nand_2_out);

  // Notes on the sheet:
  //   1 bit Memory Cell
endmodule
