// Logisim project active_low_sr_latch.circ as structural Verilog: 1 circuit, main circuit main
module main (
  input  reset,
  input  set,
  output q,
  output nq
);

  nand nand_1 (q, reset, nq);
  nand nand_2 (nq, q, set);

  // Notes on the sheet:
  //   Active Low SR Latch
endmodule
