// Logisim project active_low_sr_latch_with_enable_bit.circ as structural Verilog: 1 circuit, main circuit main
module main (
  input  set,
  input  enable,
  input  reset,
  output q,
  output nq
);

  wire nand_1_out, nand_2_out;

  nand nand_1 (nand_1_out, set, enable);
  nand nand_2 (nand_2_out, enable, reset);
  nand nand_3 (q, nand_1_out, nq);
  nand nand_4 (nq, q, nand_2_out);

  // Notes on the sheet:
  //   Active Low SR Latch with Enable bit
endmodule
