// Logisim project 2x4_Decoder.circ as structural Verilog
module CPU_MEM_1 (
  input  set,
  input  enable,
  output q
);

  wire nand_1_out, nand_2_out, nand_4_out, not_1_out;

  not not_1 (not_1_out, set);
  nand nand_1 (nand_1_out, set, enable);
  nand nand_2 (nand_2_out, enable, not_1_out);
  nand nand_3 (q, nand_1_out, nand_4_out);
  nand nand_4 (nand_4_out, q, nand_2_out);

  // Notes on the sheet:
  //   1 bit Memory Cell
endmodule

module CPU_MEM_8 (
  input  [7:0] in_1,
  input  set,
  output [7:0] out_3
);

  CPU_MEM_1 cpu_mem_1_1 (.set(in_1[0]), .enable(set), .q(out_3[0]));
  CPU_MEM_1 cpu_mem_1_2 (.set(in_1[1]), .enable(set), .q(out_3[1]));
  CPU_MEM_1 cpu_mem_1_3 (.set(in_1[2]), .enable(set), .q(out_3[2]));
  CPU_MEM_1 cpu_mem_1_4 (.set(in_1[3]), .enable(set), .q(out_3[3]));
  CPU_MEM_1 cpu_mem_1_5 (.set(in_1[4]), .enable(set), .q(out_3[4]));
  CPU_MEM_1 cpu_mem_1_6 (.set(in_1[5]), .enable(set), .q(out_3[5]));
  CPU_MEM_1 cpu_mem_1_7 (.set(in_1[6]), .enable(set), .q(out_3[6]));
  CPU_MEM_1 cpu_mem_1_8 (.set(in_1[7]), .enable(set), .q(out_3[7]));
endmodule

module CPU_REG (
  input  [7:0] in_1,
  input  in_2,
  input  in_3,
  output [7:0] out_4
);

  wire [7:0] cpu_mem_8_1_out_3;

  CPU_MEM_8 cpu_mem_8_1 (.in_1(in_1), .out_3(cpu_mem_8_1_out_3), .set(in_2));
  CPU_ENABLE cpu_enable_1 (.in_1(cpu_mem_8_1_out_3), .out_3(out_4), .set(in_3));
endmodule

module CPU_ENABLE (
  input  [7:0] in_1,
  input  set,
  output [7:0] out_3
);

  and and_1 (out_3[0], in_1[0], set);
  and and_2 (out_3[1], in_1[1], set);
  and and_3 (out_3[2], in_1[2], set);
  and and_4 (out_3[3], in_1[3], set);
  and and_5 (out_3[4], in_1[4], set);
  and and_6 (out_3[5], in_1[5], set);
  and and_7 (out_3[6], in_1[6], set);
  and and_8 (out_3[7], in_1[7], set);
endmodule

module CPU_DECODER_2x4 (
  input  A,
  input  B,
  output [3:0] out_3
);

  wire not_1_out, not_2_out;

  not not_1 (not_1_out, A);
  not not_2 (not_2_out, B);
  buf _00 (out_3[0], not_1_out);  // AND_Gate
  and _01 (out_3[1], not_1_out, B);
  and _10 (out_3[2], A, not_2_out);
  and _11 (out_3[3], A, B);
endmodule
