// Logisim project 4_bit_memory.circ as structural Verilog: 2 circuits, main circuit main
module main (
  input  [3:0] in_1,
  input  in_2,
  input  in_3,
  input  [3:0] in_4,
  output out_5,
  output out_6,
  output out_7,
  output out_8,
  output out_9
);

  nand_not nand_not_1 (.in_1(in_2), .in_2(in_3), .out_3(out_7));
  nand_not nand_not_2 (.in_1(in_1[0]), .in_2(in_4[0]), .out_3(out_5));
  nand_not nand_not_3 (.in_1(in_1[1]), .in_2(in_4[1]), .out_3(out_6));
  nand_not nand_not_4 (.in_1(in_1[2]), .in_2(in_4[2]), .out_3(out_8));
  nand_not nand_not_5 (.in_1(in_1[3]), .in_2(in_4[3]), .out_3(out_9));
endmodule

module nand_not (
  input  in_1,
  input  in_2,
  output out_3
);

  wire nand_1_out;

  nand nand_1 (nand_1_out, in_1, in_2);
  not not_1 (out_3, nand_1_out);
endmodule
