// Logisim project 8_bit_memory_cell.circ as structural Verilog
module CPU_MEM_1 (
  input  set,
  input  enable,
  output q
);

  wire nand_1_out, nand_2_out, nand_4_out, not_1_out;

  not not_1 (not_1_out, set);
  nand nand_1 (nand_1_out, set, enable);
  nand nand_2 (nand_2_out, enable, not_1_out);
  nand nand_3 (q, nand_1_out, nand_4_out);
  nand nand_4 (nand_4_out, q, nand_2_out);

  // Notes on the sheet:
  //   1 bit Memory Cell
endmodule

module CPU_MEM_8 (
  input  [7:0] in_1,
  input  set,
  output [7:0] out_3
);

  CPU_MEM_1 cpu_mem_1_1 (.set(in_1[0]), .enable(set), .q(out_3[0]));
  CPU_MEM_1 cpu_mem_1_2 (.set(in_1[1]), .enable(set), .q(out_3[1]));
  CPU_MEM_1 cpu_mem_1_3 (.set(in_1[2]), .enable(set), .q(out_3[2]));
  CPU_MEM_1 cpu_mem_1_4 (.set(in_1[3]), .enable(set), .q(out_3[3]));
  CPU_MEM_1 cpu_mem_1_5 (.set(in_1[4]), .enable(set), .q(out_3[4]));
  CPU_MEM_1 cpu_mem_1_6 (.set(in_1[5]), .enable(set), .q(out_3[5]));
  CPU_MEM_1 cpu_mem_1_7 (.set(in_1[6]), .enable(set), .q(out_3[6]));
  CPU_MEM_1 cpu_mem_1_8 (.set(in_1[7]), .enable(set), .q(out_3[7]));
endmodule
