// Logisim project control_buffer.circ as structural Verilog: 1 circuit, main circuit main
module main (
  input  in_1,
  input  in_2,
  input  in_3,
  input  in_4,
  output out_5
);

  wire and_1_out, and_2_out, button_1_out, button_2_out;

  and and_1 (and_1_out, in_1, in_2);
  and and_2 (and_2_out, in_3, in_4);
  Button button_1 (.out(button_1_out));
  assign out_5 = button_1_out ? and_1_out : 1'bz;  // Controlled_Buffer controlled_buffer_1
  assign out_5 = button_2_out ? and_2_out : 1'bz;  // Controlled_Buffer controlled_buffer_2
  Button button_2 (.out(button_2_out));
endmodule
