// Logisim project nand_not.circ as structural Verilog: 1 circuit, main circuit main
module main (
  output out_1
);

  wire nand_1_out, tunnel;

  Clock clock_1 (.out(tunnel));
  not not_1 (out_1, nand_1_out);
  nand nand_1 (nand_1_out, tunnel, tunnel);
endmodule
